# Fritzing sketch Sketch (saved by Fritzing 0.9.3b)

parts:
  U1 = ESP32S-HiLetgo [part_number=ESP32S-HiLetgo]
  Bauteil1 = Thumb Joystick

nets:
  N1: U1.3.3, Bauteil1.VCC
  GND: U1.GND, Bauteil1.GND
  N2: U1.GPIO15, Bauteil1.SEL
  N3: U1.GPIO2, Bauteil1.VERT
  N4: U1.GPIO4, Bauteil1.HORZ

custom parts:
  ESP32S-HiLetgo: HiLetgo ESP-WROOM-32 ESP32 ESP-32S Development Board 2.4GHz Dual-Mode WiFi + Bluetooth Dual Cores Microcontroller The ESP32 integrated with Antenna switches, RF Balun, power amplifiers, low-noise amplifiers, filters, and management modules, and the entire solution occupies the least area of PCB. 2.4 GHz Wi-Fi plus Bluetooth dual-mode chip, with TSMC Ultra-low power consumption 40nm technology,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
